// Digital circuit ALU.dig as structural Verilog
module ALU (
  input  [3:0] A,
  input  [2:0] OP,
  input  [3:0] B,
  input  Cin,
  input  DIsable_Out
);

  wire And0, And1, And2, And3, B_or_Const_pin1, B_or_Const_pin4, B_or_Const_pin7, B_or_Const_pin9,
       B_or_Const_pin12, Cin_or_Sub_pin3, Cout, ExtCout, ExtNout, ExtOut0, ExtOut1, ExtOut2, ExtOut3,
       ExtVout, ExtZout, Not0, Not1, Not2, Not3, Not_pin11, Not_pin13, NotA3, NotB3, NotOut3, Ones_Comp_pin2,
       Ones_Comp_pin3, Ones_Comp_pin6, Ones_Comp_pin8, Ones_Comp_pin11, OPadd, OPand, OPdec, OPinc, OPnot,
       OPor, OPsub, OPxor, Or0, Or1, Or2, Or3, Out0, Out1, Out2, Out3, Overflow_1_pin6, Overflow_1_pin12,
       Sum0, Sum1, Sum2, Sum3, Vout, XOr0, XOr1, XOr2, XOr3, Zout;

  Seven_Seg_Hex seven_seg_hex_1 (.d(A), .dp(1'b0));
  Seven_Seg_Hex seven_seg_hex_2 (.d(B), .dp(1'b0));
  _74238 Op_Decoder (
    .pin1(OP[0]), .pin2(OP[1]), .pin3(OP[2]), .pin4(1'b0), .pin5(1'b0), .pin6(1'b1), .pin7(OPdec),
    .pin8(1'b0), .pin9(OPinc), .pin10(OPsub), .pin11(OPadd), .pin12(OPxor), .pin13(OPnot), .pin14(OPor),
    .pin15(OPand), .pin16(1'b1));
  LED C (.in(ExtCout));
  LED N (.in(ExtNout));
  LED Z (.in(ExtZout));
  LED V (.in(ExtVout));
  Seven_Seg_Hex seven_seg_hex_3 (.d({ExtOut3, ExtOut2, ExtOut1, ExtOut0}), .dp(1'b0));
  LED led_1 (.in(ExtOut3));
  _74157 B_or_Const (
    .pin1(B_or_Const_pin1), .pin2(B[0]), .pin3(1'b1), .pin4(B_or_Const_pin4), .pin5(B[1]), .pin6(1'b0),
    .pin7(B_or_Const_pin7), .pin8(1'b0), .pin9(B_or_Const_pin9), .pin10(1'b0), .pin11(B[2]),
    .pin12(B_or_Const_pin12), .pin13(1'b0), .pin14(B[3]), .pin15(1'b0), .pin16(1'b1));
  LED led_2 (.in(ExtOut2));
  _74151 Bit_3_Mux (
    .pin1(XOr3), .pin2(Not3), .pin3(Or3), .pin4(And3), .pin5(Out3), .pin7(1'b0), .pin8(1'b0), .pin9(OP[2]),
    .pin10(OP[1]), .pin11(OP[0]), .pin12(Sum3), .pin13(Sum3), .pin14(Sum3), .pin15(Sum3), .pin16(1'b1));  // open: pin6
  LED led_3 (.in(ExtOut1));
  LED led_4 (.in(ExtOut0));
  _7408 And (
    .pin1(A[0]), .pin2(B[0]), .pin3(And0), .pin4(A[1]), .pin5(B[1]), .pin6(And1), .pin7(1'b0), .pin8(And2),
    .pin9(A[2]), .pin10(B[2]), .pin11(And3), .pin12(A[3]), .pin13(B[3]), .pin14(1'b1));
  _7486 Ones_Comp (
    .pin1(B_or_Const_pin4), .pin2(Ones_Comp_pin2), .pin3(Ones_Comp_pin3), .pin4(B_or_Const_pin7),
    .pin5(Ones_Comp_pin2), .pin6(Ones_Comp_pin6), .pin7(1'b0), .pin8(Ones_Comp_pin8), .pin9(B_or_Const_pin9),
    .pin10(Ones_Comp_pin2), .pin11(Ones_Comp_pin11), .pin12(B_or_Const_pin12), .pin13(Ones_Comp_pin2),
    .pin14(1'b1));
  _7432 Cin_or_Sub (
    .pin1(Ones_Comp_pin2), .pin2(Cin), .pin3(Cin_or_Sub_pin3), .pin4(OPsub), .pin5(OPdec),
    .pin6(Ones_Comp_pin2), .pin7(1'b0), .pin8(B_or_Const_pin1), .pin9(OPdec), .pin10(OPinc), .pin12(1'b0),
    .pin13(1'b0), .pin14(1'b1));  // open: pin11
  _74151 Bit_2_Mux (
    .pin1(XOr2), .pin2(Not2), .pin3(Or2), .pin4(And2), .pin5(Out2), .pin7(1'b0), .pin8(1'b0), .pin9(OP[2]),
    .pin10(OP[1]), .pin11(OP[0]), .pin12(Sum2), .pin13(Sum2), .pin14(Sum2), .pin15(Sum2), .pin16(1'b1));  // open: pin6
  _7432 Or (
    .pin1(A[0]), .pin2(B[0]), .pin3(Or0), .pin4(A[1]), .pin5(B[1]), .pin6(Or1), .pin7(1'b0), .pin8(Or2),
    .pin9(A[2]), .pin10(B[2]), .pin11(Or3), .pin12(A[3]), .pin13(B[3]), .pin14(1'b1));
  _7483 Full_Adder (
    .pin1(A[3]), .pin2(Sum2), .pin3(A[2]), .pin4(Ones_Comp_pin8), .pin5(1'b1), .pin6(Sum1),
    .pin7(Ones_Comp_pin6), .pin8(A[1]), .pin9(Sum0), .pin10(A[0]), .pin11(Ones_Comp_pin3), .pin12(1'b0),
    .pin13(Cin_or_Sub_pin3), .pin14(Cout), .pin15(Sum3), .pin16(Ones_Comp_pin11));
  _74151 Bit_1_Mux (
    .pin1(XOr1), .pin2(Not1), .pin3(Or1), .pin4(And1), .pin5(Out1), .pin7(1'b0), .pin8(1'b0), .pin9(OP[2]),
    .pin10(OP[1]), .pin11(OP[0]), .pin12(Sum1), .pin13(Sum1), .pin14(Sum1), .pin15(Sum1), .pin16(1'b1));  // open: pin6
  _7486 Xor (
    .pin1(A[0]), .pin2(B[0]), .pin3(XOr0), .pin4(A[1]), .pin5(B[1]), .pin6(XOr1), .pin7(1'b0), .pin8(XOr2),
    .pin9(A[2]), .pin10(B[2]), .pin11(XOr3), .pin12(A[3]), .pin13(B[3]), .pin14(1'b1));
  _74151 Bit_0_Mux (
    .pin1(XOr0), .pin2(Not0), .pin3(Or0), .pin4(And0), .pin5(Out0), .pin7(1'b0), .pin8(1'b0), .pin9(OP[2]),
    .pin10(OP[1]), .pin11(OP[0]), .pin12(Sum0), .pin13(Sum0), .pin14(Sum0), .pin15(Sum0), .pin16(1'b1));  // open: pin6
  _7425 Zero (
    .pin1(Out0), .pin2(Out1), .pin4(Out2), .pin5(Out3), .pin6(Zout), .pin7(1'b0), .pin9(1'b0), .pin10(1'b0),
    .pin12(1'b0), .pin13(1'b0), .pin14(1'b1));  // open: pin3, pin8, pin11
  _7410 Overflow_1 (
    .pin1(A[3]), .pin2(B[3]), .pin3(NotA3), .pin4(NotB3), .pin5(Out3), .pin6(Overflow_1_pin6), .pin7(1'b0),
    .pin9(1'b0), .pin10(1'b0), .pin11(1'b0), .pin12(Overflow_1_pin12), .pin13(NotOut3), .pin14(1'b1));  // open: pin8
  _7404 Not (
    .pin1(A[0]), .pin2(Not0), .pin3(A[1]), .pin4(Not1), .pin5(A[2]), .pin6(Not2), .pin7(1'b0), .pin8(Not3),
    .pin9(A[3]), .pin11(Not_pin11), .pin13(Not_pin13), .pin14(1'b1));  // open: pin10, pin12
  _74245 Tri_State_Result (
    .pin1(1'b1), .pin2(Out0), .pin3(Out1), .pin4(Out2), .pin5(Out3), .pin6(Cout), .pin7(Out3), .pin8(Zout),
    .pin9(Vout), .pin10(1'b0), .pin11(ExtVout), .pin12(ExtZout), .pin13(ExtNout), .pin14(ExtCout),
    .pin15(ExtOut3), .pin16(ExtOut2), .pin17(ExtOut1), .pin18(ExtOut0), .pin19(DIsable_Out), .pin20(1'b1));
  // NotConnected on Not_pin13
  // NotConnected on Not_pin11
  _7400 Overflow_2 (
    .pin1(A[3]), .pin2(A[3]), .pin3(NotA3), .pin4(B[3]), .pin5(B[3]), .pin6(NotB3), .pin7(1'b0),
    .pin8(NotOut3), .pin9(Out3), .pin10(Out3), .pin11(Vout), .pin12(Overflow_1_pin6),
    .pin13(Overflow_1_pin12), .pin14(1'b1));

  // Other names for the same wires on the sheet: DisableOut = DIsable_Out

  // Notes on the sheet:
  //   A: default 3
  //   B: default 2
  //   In
  //   Out
endmodule
