// Digital circuit CPU.dig as structural Verilog
module CPU (
);

  wire _8_bit_alu_1_p1, _8_bit_alu_1_p2;

  Register A ();  // open: C, D, OUT, LD, Q, lt_Q_gt
  Register B ();  // open: C, D, OUT, LD, Q, lt_Q_gt
  // _8_Bit_ALU _8_bit_alu_1: pin names not known; wires that end beside it: _8_bit_alu_1_p1, _8_bit_alu_1_p2, _8_bit_alu_1_p1, _8_bit_alu_1_p2
endmodule
