// Digital circuit RAM.dig as structural Verilog
module RAM (
  input  [3:0] Addr,
  input  Store,
  input  Output,
  input  [3:0] Data_In,
  input  Store_2,
  input  [12:0] Addr_2,
  input  [7:0] Data_In_2,
  output [3:0] Data_Out,
  output [7:0] Data_Out_2
);

  wire a623308a_1_p15, Clock_out;

  // A623308A a623308a_1: pin names not known; wires that end beside it: Addr_2[12], Addr_2[7], Addr_2[6], Addr_2[5], Addr_2[4], Addr_2[3], Addr_2[2], Addr_2[1], Addr_2[0], Data_Out_2[0], Data_Out_2[1], Data_Out_2[2], 1'b0, 1'b1, a623308a_1_p15, Addr_2[8], Addr_2[9], Addr_2[11], Store_2, Addr_2[10], 1'b0, Data_Out_2[7]
  not not_1 (a623308a_1_p15, Store_2);
  assign Data_Out_2 = Store_2 ? Data_In_2 : 8'bz;  // Driver driver_1
  Button Clock (.out(Clock_out));
  RAMSinglePort #(.AddrBits(4), .Bits(4)) ramsingleport_1 (
    .A(Addr), .str(Store), .C(Clock_out), .ld(Output), .D(Data_Out));
  assign Data_Out = Store ? Data_In : 4'bz;  // Driver driver_2
endmodule
