// Digital circuit 74-ALU.dig as structural Verilog
module _74_ALU (
  input  [7:0] A,
  input  [7:0] B,
  input  [2:0] OP,
  input  CIN,
  output [7:0] OUT,
  output VOUT,
  output COUT
);

  wire _3_Input_NANDs_pin6, _3_Input_NANDs_pin12, AND0, AND1, AND2, AND3, AND4, AND5, AND6, AND7, B1SNEG,
       Full_Adder_pin14, MUX_2_pin1, MUX_2_pin4, MUX_2_pin7, MUX_2_pin9, MUX_2_pin12, MUX_3_pin4, MUX_3_pin7,
       MUX_3_pin9, MUX_3_pin12, NOT0, NOT1, NOT2, NOT3, NOT4, NOT5, NOT6, NOT7, NOTA7, NOTB1SNEG, NOTOUT7,
       OPADD, OPAND, OPDEC, OPINC, OPNOT, OPOR, OPSUB, OPXOR, OR0, OR1, OR2, OR3, OR4, OR5, OR6, OR7,
       OR_2_pin3, OR_2_pin11, OR_2_pin13, SUM0, SUM1, SUM2, SUM3, SUM4, SUM5, SUM6, SUM7, XOR0, XOR1, XOR2,
       XOR3, XOR4, XOR5, XOR6, XOR7, XOR_2_pin2, XOR_2_pin3, XOR_2_pin6, XOR_2_pin8, XOR_2_pin11, XOR_3_pin3,
       XOR_3_pin6, XOR_3_pin8;

  LED led_1 (.in(A[7]));
  Seven_Seg_Hex seven_seg_hex_1 (.d(A[3:0]), .dp(1'b0));
  Seven_Seg_Hex seven_seg_hex_2 (.d(A[7:4]), .dp(1'b0));
  LED led_2 (.in(A[6]));
  LED led_3 (.in(A[5]));
  LED led_4 (.in(A[4]));
  LED led_5 (.in(A[3]));
  LED AND (.in(OPAND));
  LED OR (.in(OPOR));
  LED NOT (.in(OPNOT));
  LED XOR (.in(OPXOR));
  LED ADD (.in(OPADD));
  LED SUB (.in(OPSUB));
  LED INC (.in(OPINC));
  LED DEC (.in(OPDEC));
  LED led_6 (.in(A[2]));
  LED led_7 (.in(A[1]));
  LED led_8 (.in(A[0]));
  LED led_9 (.in(B[7]));
  LED led_10 (.in(OUT[7]));
  LED led_11 (.in(OUT[6]));
  Seven_Seg_Hex seven_seg_hex_3 (.d(B[3:0]), .dp(1'b0));
  Seven_Seg_Hex seven_seg_hex_4 (.d(B[7:4]), .dp(1'b0));
  LED led_12 (.in(B[6]));
  LED led_13 (.in(B[5]));
  LED led_14 (.in(B[4]));
  LED led_15 (.in(B[3]));
  Seven_Seg_Hex seven_seg_hex_5 (.d(OUT[3:0]), .dp(1'b0));
  Seven_Seg_Hex seven_seg_hex_6 (.d(OUT[7:4]), .dp(1'b0));
  LED led_16 (.in(OUT[5]));
  LED led_17 (.in(OUT[4]));
  LED led_18 (.in(OUT[3]));
  LED led_19 (.in(OUT[2]));
  LED led_20 (.in(B[2]));
  LED led_21 (.in(B[1]));
  LED led_22 (.in(B[0]));
  LED led_23 (.in(OUT[1]));
  LED led_24 (.in(OUT[0]));
  LED led_25 (.in(CIN));
  LED led_26 (.in(VOUT));
  LED led_27 (.in(COUT));
  _74238 MUX (
    .pin1(OP[0]), .pin2(OP[1]), .pin3(OP[2]), .pin4(1'b0), .pin5(1'b0), .pin6(1'b1), .pin7(OPDEC),
    .pin8(1'b0), .pin9(OPINC), .pin10(OPSUB), .pin11(OPADD), .pin12(OPXOR), .pin13(OPNOT), .pin14(OPOR),
    .pin15(OPAND), .pin16(1'b1));
  _74157 MUX_2 (
    .pin1(MUX_2_pin1), .pin2(B[0]), .pin3(1'b1), .pin4(MUX_2_pin4), .pin5(B[1]), .pin6(1'b0),
    .pin7(MUX_2_pin7), .pin8(1'b0), .pin9(MUX_2_pin9), .pin10(1'b0), .pin11(B[2]), .pin12(MUX_2_pin12),
    .pin13(1'b0), .pin14(B[3]), .pin15(1'b0), .pin16(1'b1));
  _74157 MUX_3 (
    .pin1(MUX_2_pin1), .pin2(B[4]), .pin3(1'b0), .pin4(MUX_3_pin4), .pin5(B[5]), .pin6(1'b0),
    .pin7(MUX_3_pin7), .pin8(1'b0), .pin9(MUX_3_pin9), .pin10(1'b0), .pin11(B[6]), .pin12(MUX_3_pin12),
    .pin13(1'b0), .pin14(B[7]), .pin15(1'b0), .pin16(1'b1));
  _7408 And_Low (
    .pin1(A[0]), .pin2(B[0]), .pin3(AND0), .pin4(A[1]), .pin5(B[1]), .pin6(AND1), .pin7(1'b0), .pin8(AND2),
    .pin9(A[2]), .pin10(B[2]), .pin11(AND3), .pin12(A[3]), .pin13(B[3]), .pin14(1'b1));
  _7408 And_High (
    .pin1(A[4]), .pin2(B[4]), .pin3(AND4), .pin4(A[5]), .pin5(B[5]), .pin6(AND5), .pin7(1'b0), .pin8(AND6),
    .pin9(A[6]), .pin10(B[6]), .pin11(AND7), .pin12(A[7]), .pin13(B[7]), .pin14(1'b1));
  _7432 Or_Low (
    .pin1(A[0]), .pin2(B[0]), .pin3(OR0), .pin4(A[1]), .pin5(B[1]), .pin6(OR1), .pin7(1'b0), .pin8(OR2),
    .pin9(A[2]), .pin10(B[2]), .pin11(OR3), .pin12(A[3]), .pin13(B[3]), .pin14(1'b1));
  _7432 Or_High (
    .pin1(A[4]), .pin2(B[4]), .pin3(OR4), .pin4(A[5]), .pin5(B[5]), .pin6(OR5), .pin7(1'b0), .pin8(OR6),
    .pin9(A[6]), .pin10(B[6]), .pin11(OR7), .pin12(A[7]), .pin13(B[7]), .pin14(1'b1));
  _7486 XOR_2 (
    .pin1(MUX_2_pin4), .pin2(XOR_2_pin2), .pin3(XOR_2_pin3), .pin4(MUX_2_pin7), .pin5(XOR_2_pin2),
    .pin6(XOR_2_pin6), .pin7(1'b0), .pin8(XOR_2_pin8), .pin9(MUX_2_pin9), .pin10(XOR_2_pin2),
    .pin11(XOR_2_pin11), .pin12(MUX_2_pin12), .pin13(XOR_2_pin2), .pin14(1'b1));
  _7486 XOR_3 (
    .pin1(MUX_3_pin4), .pin2(XOR_2_pin2), .pin3(XOR_3_pin3), .pin4(MUX_3_pin7), .pin5(XOR_2_pin2),
    .pin6(XOR_3_pin6), .pin7(1'b0), .pin8(XOR_3_pin8), .pin9(MUX_3_pin9), .pin10(XOR_2_pin2), .pin11(B1SNEG),
    .pin12(MUX_3_pin12), .pin13(XOR_2_pin2), .pin14(1'b1));
  _7432 OR_2 (
    .pin1(OPADD), .pin2(OPSUB), .pin3(OR_2_pin3), .pin4(OPSUB), .pin5(OPDEC), .pin6(XOR_2_pin2), .pin7(1'b0),
    .pin8(MUX_2_pin1), .pin9(OPDEC), .pin10(OPINC), .pin11(OR_2_pin11), .pin12(OPDEC), .pin13(OR_2_pin13),
    .pin14(1'b1));
  _7486 Xor_Low (
    .pin1(A[0]), .pin2(B[0]), .pin3(XOR0), .pin4(A[1]), .pin5(B[1]), .pin6(XOR1), .pin7(1'b0), .pin8(XOR2),
    .pin9(A[2]), .pin10(B[2]), .pin11(XOR3), .pin12(A[3]), .pin13(B[3]), .pin14(1'b1));
  _7486 Xor_High (
    .pin1(A[4]), .pin2(B[4]), .pin3(XOR4), .pin4(A[5]), .pin5(B[5]), .pin6(XOR5), .pin7(1'b0), .pin8(XOR6),
    .pin9(A[6]), .pin10(B[6]), .pin11(XOR7), .pin12(A[7]), .pin13(B[7]), .pin14(1'b1));
  _7483 Full_Adder (
    .pin1(A[3]), .pin2(SUM2), .pin3(A[2]), .pin4(XOR_2_pin8), .pin5(1'b1), .pin6(SUM1), .pin7(XOR_2_pin6),
    .pin8(A[1]), .pin9(SUM0), .pin10(A[0]), .pin11(XOR_2_pin3), .pin12(1'b0), .pin13(OR_2_pin11),
    .pin14(Full_Adder_pin14), .pin15(SUM3), .pin16(XOR_2_pin11));
  _7483 Full_Adder_2 (
    .pin1(A[7]), .pin2(SUM6), .pin3(A[6]), .pin4(XOR_3_pin8), .pin5(1'b1), .pin6(SUM5), .pin7(XOR_3_pin6),
    .pin8(A[5]), .pin9(SUM4), .pin10(A[4]), .pin11(XOR_3_pin3), .pin12(1'b0), .pin13(Full_Adder_pin14),
    .pin14(COUT), .pin15(SUM7), .pin16(B1SNEG));
  _7408 AND_2 (
    .pin1(CIN), .pin2(OR_2_pin3), .pin3(OR_2_pin13), .pin4(1'b0), .pin5(1'b0), .pin7(1'b0), .pin9(1'b0),
    .pin10(1'b0), .pin12(1'b0), .pin13(1'b0), .pin14(1'b1));  // open: pin6, pin8, pin11
  _7404 Not_2 (
    .pin1(A[0]), .pin2(NOT0), .pin3(A[1]), .pin4(NOT1), .pin5(A[2]), .pin6(NOT2), .pin7(1'b0), .pin8(NOT3),
    .pin9(A[3]), .pin11(1'b0), .pin13(1'b0), .pin14(1'b1));  // open: pin10, pin12
  _7404 Not_3 (
    .pin1(A[4]), .pin2(NOT4), .pin3(A[5]), .pin4(NOT5), .pin5(A[6]), .pin6(NOT6), .pin7(1'b0), .pin8(NOT7),
    .pin9(A[7]), .pin11(1'b0), .pin13(1'b0), .pin14(1'b1));  // open: pin10, pin12
  _7410 _3_Input_NANDs (
    .pin1(A[7]), .pin2(B1SNEG), .pin3(NOTA7), .pin4(NOTB1SNEG), .pin5(OUT[7]), .pin6(_3_Input_NANDs_pin6),
    .pin7(1'b0), .pin9(1'b0), .pin10(1'b0), .pin11(1'b0), .pin12(_3_Input_NANDs_pin12), .pin13(NOTOUT7),
    .pin14(1'b1));  // open: pin8
  _74151 Bit_3_Mux (
    .pin1(XOR3), .pin2(NOT3), .pin3(OR3), .pin4(AND3), .pin5(OUT[3]), .pin7(1'b0), .pin8(1'b0), .pin9(OP[2]),
    .pin10(OP[1]), .pin11(OP[0]), .pin12(SUM3), .pin13(SUM3), .pin14(SUM3), .pin15(SUM3), .pin16(1'b1));  // open: pin6
  _74151 Bit_7_Mux (
    .pin1(XOR7), .pin2(NOT7), .pin3(OR7), .pin4(AND7), .pin5(OUT[7]), .pin7(1'b0), .pin8(1'b0), .pin9(OP[2]),
    .pin10(OP[1]), .pin11(OP[0]), .pin12(SUM7), .pin13(SUM7), .pin14(SUM7), .pin15(SUM7), .pin16(1'b1));  // open: pin6
  _7400 _2_Input_NANDs (
    .pin1(A[7]), .pin2(A[7]), .pin3(NOTA7), .pin4(B1SNEG), .pin5(B1SNEG), .pin6(NOTB1SNEG), .pin7(1'b0),
    .pin8(NOTOUT7), .pin9(OUT[7]), .pin10(OUT[7]), .pin11(VOUT), .pin12(_3_Input_NANDs_pin6),
    .pin13(_3_Input_NANDs_pin12), .pin14(1'b1));
  _74151 Bit_2_Mux (
    .pin1(XOR2), .pin2(NOT2), .pin3(OR2), .pin4(AND2), .pin5(OUT[2]), .pin7(1'b0), .pin8(1'b0), .pin9(OP[2]),
    .pin10(OP[1]), .pin11(OP[0]), .pin12(SUM2), .pin13(SUM2), .pin14(SUM2), .pin15(SUM2), .pin16(1'b1));  // open: pin6
  _74151 Bit_6_Mux (
    .pin1(XOR6), .pin2(NOT6), .pin3(OR6), .pin4(AND6), .pin5(OUT[6]), .pin7(1'b0), .pin8(1'b0), .pin9(OP[2]),
    .pin10(OP[1]), .pin11(OP[0]), .pin12(SUM6), .pin13(SUM6), .pin14(SUM6), .pin15(SUM6), .pin16(1'b1));  // open: pin6
  _74151 Bit_1_Mux (
    .pin1(XOR1), .pin2(NOT1), .pin3(OR1), .pin4(AND1), .pin5(OUT[1]), .pin7(1'b0), .pin8(1'b0), .pin9(OP[2]),
    .pin10(OP[1]), .pin11(OP[0]), .pin12(SUM1), .pin13(SUM1), .pin14(SUM1), .pin15(SUM1), .pin16(1'b1));  // open: pin6
  _74151 Bit_5_Mux (
    .pin1(XOR5), .pin2(NOT5), .pin3(OR5), .pin4(AND5), .pin5(OUT[5]), .pin7(1'b0), .pin8(1'b0), .pin9(OP[2]),
    .pin10(OP[1]), .pin11(OP[0]), .pin12(SUM5), .pin13(SUM5), .pin14(SUM5), .pin15(SUM5), .pin16(1'b1));  // open: pin6
  _74151 Bit_0_Mux (
    .pin1(XOR0), .pin2(NOT0), .pin3(OR0), .pin4(AND0), .pin5(OUT[0]), .pin7(1'b0), .pin8(1'b0), .pin9(OP[2]),
    .pin10(OP[1]), .pin11(OP[0]), .pin12(SUM0), .pin13(SUM0), .pin14(SUM0), .pin15(SUM0), .pin16(1'b1));  // open: pin6
  _74151 Bit_4_Mux (
    .pin1(XOR4), .pin2(NOT4), .pin3(OR4), .pin4(AND4), .pin5(OUT[4]), .pin7(1'b0), .pin8(1'b0), .pin9(OP[2]),
    .pin10(OP[1]), .pin11(OP[0]), .pin12(SUM4), .pin13(SUM4), .pin14(SUM4), .pin15(SUM4), .pin16(1'b1));  // open: pin6

  // Other names for the same wires on the sheet: CCALC = COUT; CINT = CIN; VCALC = VOUT

  // Notes on the sheet:
  //   A: default 3
  //   B: default 2
  //   NOTES
  //   Will the fan out from the SUB or DEC "or"
  //   be an issue if we use TTL?
  //   Follows the 6502 sub behaviour where CIN
  //   must be set for correct substraction
  //   0 0 0 AND
  //   0 0 1 OR
  //   0 1 0 NOT
  //   0 1 1 XOR
  //   1 0 0 ADD
  //   1 0 1 SUB
  //   1 1 0 INC
  //   1 1 1 DEC
  //   A
  //   Out
  //   B
  //   Op Decoding
  //   Arithmetic Operations
  //   (OPADD OR OPSUB) AND CIN => CIN Adder
  //    OPSUB OR OPDEC => 1's Comp
  //    OPINC OR OPDDEC =>  '1' else B
  //   B or 1 constant 
  //   for Inc/Dec
  //   Logical Operations
  //   (B or 1) 1's compliment for SUB/SEC
  //   by Xoring with OPSUB or DEC
  //   SUB or DEC
  //   ADD or SUB
  //   INC or DEC
  //   Use CIN only for ADD/SUB
  //   NOT ANEG AND NOT B1SNEG AND OUTNEG
  //   OR
  //   ANEG AND B1SNEG AND NOT OUTNEXT
  //   Note B1SNEG is B7 after being 1's complemented for sub/dec operations
  //   Derivation in NAND Logic
  //   NOT ((NOT (NOT ANEG  AND NOT B1SNEG AND OUTNEG)) AND (NOT (ANEG AND B1SNEG AND NOT OUTNEXT)))
  //   NAND(NAND (NOT ANEG, NOT B1SNEG, OUTNEG), NAND (ANEG, B1SNEG, NOT OUTNEXT))
  //   Overflow
  //   Data Output Selection
endmodule

/* Test case AND:
A    B    OP   CIN OUT  COUT VOUT
0x00 0x00 0x00 0   0    X    X
0x00 0x00 0x00 1   0    X    X
0xBE 0xAC 0x00 0   0xAC X    X
0xBE 0xAC 0x00 1   0xAC X    X
*/

/* Test case NOT:
A    B    OP  CIN OUT  COUT VOUT
0x00 0x00 0x2 0   0xFF X    X
0x00 0x00 0x2 1   0xFF X    X
0xBE 0xC5 0x2 0   0x41 X    X
0xBE 0xAC 0x2 1   0x41 X    X
*/

/* Test case ADD:
A    B    OP  CIN OUT  COUT VOUT
0x01 0x02 0x4 0   0x03 0    0
0xA0 0x12 0x4 0   0xB2 0    0
0xCC 0xDE 0x4 0   0xAA 1    0
0xCC 0xBB 0x4 0   0x87 1    0
# Two positives creating a negative
0x50 0x55 0x4 0   0xA5 0    1
# Two negatives create a positive
0xF0 0x80 0x4 0   0x70 1    1
*/

/* Test case INC:
A    B    OP  CIN OUT  COUT VOUT
0x01 0x02 0x6 0   0x02 0    X
0x01 0x04 0x6 0   0x02 0    X
0x01 0x02 0x6 1   0x02 0    X
0x01 0x04 0x6 1   0x02 0    X
0xCC 0x02 0x6 0   0xCD 0    X
0xFF 0x00 0x6 0   0x00 1    X
*/

/* Test case OR:
A    B    OP   CIN OUT  COUT VOUT
0x00 0x00 0x01 0   0    X    X
0x00 0x00 0x01 1   0    X    X
0x2E 0xAC 0x01 0   0xAE X    X
0x2E 0xAC 0x01 1   0xAE X    X
*/

/* Test case XOR:
A    B    OP  CIN OUT  COUT VOUT
0x00 0x00 0x3 0   0    X    X
0x00 0x00 0x3 1   0    X    X
0xBE 0xAC 0x3 0   0x12 X    X
0xBE 0xAC 0x3 1   0x12 X    X
*/

/* Test case SUB TODO:
A    B    OP  CIN OUT  COUT VOUT
0x01 0x02 0x4 0   0x03 0    0
0xA0 0x12 0x4 0   0xB2 0    0
0xCC 0xDE 0x4 0   0xAA 1    0
0xCC 0xBB 0x4 0   0x87 1    0
# Two positives creating a negative
0x50 0x55 0x4 0   0xA5 0    1
# Two negatives create a positive
0xF0 0x80 0x4 0   0x70 1    1
*/

/* Test case DEC:
A    B    OP  CIN OUT  COUT VOUT
0xEE 0x02 0x7 0   0xED 1    0
0xEE 0x04 0x7 0   0xED 1    0
0xEE 0x02 0x7 1   0xED 1    0
0xEE 0x04 0x7 1   0xED 1    0
0x00 0x00 0x7 0   0xFF 0    0
*/
