// Digital circuit ALU.dig as structural Verilog
module ALU (
  input  [7:0] A,
  input  [7:0] B,
  input  [2:0] OP,
  input  CIN,
  output [7:0] OUT,
  output NOUT,
  output VOUT,
  output ZOUT,
  output COUT
);

  wire ADDCOUT, and_2_out, OPADD, OPAND, OPDEC, OPINC, OPNOT, OPOR, OPSUB, OPXOR, SUBCOUT;
  wire [7:0] add_1_s, add_2_s, and_1_out, multiplexer_1_out, multiplexer_2_out, not_1_out, not_2_out,
       or_1_out, xor_1_out;

  Decoder #(.Selector_Bits(3)) decoder_1 (
    .sel(OP), .out_0(OPAND), .out_1(OPOR), .out_2(OPNOT), .out_3(OPXOR), .out_4(OPADD), .out_5(OPSUB),
    .out_6(OPINC), .out_7(OPDEC));
  Seven_Seg_Hex seven_seg_hex_1 (.d(A[7:4]), .dp(1'b0));
  Seven_Seg_Hex seven_seg_hex_2 (.d(OUT[7:4]), .dp(1'b0));
  Seven_Seg_Hex seven_seg_hex_3 (.d(A[3:0]), .dp(1'b0));
  LED led_1 (.in(A[7]));
  LED led_2 (.in(A[6]));
  LED led_3 (.in(B[7]));
  LED led_4 (.in(B[6]));
  Seven_Seg_Hex seven_seg_hex_4 (.d(OUT[3:0]), .dp(1'b0));
  LED led_5 (.in(OUT[7]));
  LED led_6 (.in(OUT[6]));
  Seven_Seg_Hex seven_seg_hex_5 (.d(B[7:4]), .dp(1'b0));
  LED led_7 (.in(A[5]));
  LED led_8 (.in(A[4]));
  LED led_9 (.in(B[5]));
  LED led_10 (.in(B[4]));
  LED led_11 (.in(OUT[5]));
  LED led_12 (.in(OUT[4]));
  Seven_Seg_Hex seven_seg_hex_6 (.d(B[3:0]), .dp(1'b0));
  LED led_13 (.in(A[3]));
  LED led_14 (.in(A[2]));
  LED led_15 (.in(B[3]));
  LED led_16 (.in(B[2]));
  LED led_17 (.in(OUT[3]));
  LED led_18 (.in(OUT[2]));
  LED led_19 (.in(A[1]));
  LED led_20 (.in(A[0]));
  LED led_21 (.in(B[1]));
  LED led_22 (.in(B[0]));
  LED N (.in(1'b0));
  LED Z (.in(1'b0));
  LED C (.in(COUT));
  LED V (.in(VOUT));
  LED led_23 (.in(OUT[1]));
  LED led_24 (.in(OUT[0]));
  Multiplexer #(.Bits(8)) multiplexer_1 (.sel(OPINC), .in_0(B), .in_1(8'h1), .out(multiplexer_1_out));
  Multiplexer #(.Bits(8)) multiplexer_2 (.sel(OPDEC), .in_0(not_1_out), .in_1({8{1'b1}}), .out(multiplexer_2_out));
  assign not_1_out = ~B;  // Not not_1, 8 bits wide
  Multiplexer #(.Selector_Bits(3)) multiplexer_3 (
    .sel(OP), .in_0(1'b0), .in_1(1'b0), .in_2(1'b0), .in_3(1'b0), .in_4(ADDCOUT), .in_5(SUBCOUT),
    .in_6(ADDCOUT), .in_7(SUBCOUT), .out(COUT));
  assign and_1_out = A & B;  // And and_1, 8 bits wide
  assign or_1_out = A | B;  // Or or_1, 8 bits wide
  assign not_2_out = ~A;  // Not not_2, 8 bits wide
  assign xor_1_out = A ^ B;  // XOr xor_1, 8 bits wide
  and and_2 (and_2_out, CIN, OPADD);
  Add #(.Bits(8)) add_1 (.a(A), .b(multiplexer_1_out), .c_i(and_2_out), .s(add_1_s), .c_o(ADDCOUT));
  Add #(.Bits(8)) add_2 (.a(A), .b(multiplexer_2_out), .c_i(OPSUB), .s(add_2_s), .c_o(SUBCOUT));
  Multiplexer #(.Selector_Bits(3)) multiplexer_4 (
    .sel(OP), .in_0(1'b0), .in_1(1'b0), .in_2(1'b0), .in_3(1'b0), .in_4(1'b0), .in_5(SUBCOUT), .in_6(1'b0),
    .in_7(SUBCOUT), .out(VOUT));
  Multiplexer #(.Selector_Bits(3), .Bits(8)) multiplexer_5 (
    .sel(OP), .in_0(and_1_out), .in_1(or_1_out), .in_2(not_2_out), .in_3(xor_1_out), .in_4(add_1_s),
    .in_5(add_2_s), .in_6(add_1_s), .in_7(add_2_s), .out(OUT));

  assign NOUT = 1'b0;
  assign ZOUT = 1'b0;

  // Notes on the sheet:
  //   A: default 80
  //   B: default 64
  //   0 0 0 AND
  //   0 0 1 OR
  //   0 1 0 NOT
  //   0 1 1 XOR
  //   1 0 0 ADD
  //   1 0 1 SUB
  //   1 1 0 INC
  //   1 1 1 DEC
  //   OUT
  //   A
  //   B
  //   Out
endmodule
