// Digital circuit Control Unit.dig as structural Verilog
module Control_Unit (
  input  [15:0] DEMODEin,
  input  [15:0] DEOPCODEin,
  input  Nin,
  input  Vin,
  input  Iin,
  input  Zin,
  input  Cin,
  input  RESET,
  input  IRQ,
  input  ClockIn,
  output [15:0] lt_uCAR_gt,
  output [15:0] lt_uParam_gt,
  output [15:0] lt_uNEXTCAR_gt,
  output [2:0] lt_uNEXTMUX_gt,
  output HALT,
  output CDATA_LD_0,
  output CDATA_LD_FF,
  output CDATA_TO_CADDRL,
  output CD_TO_CADDRH,
  output MEM_LD_XDATA,
  output MEM_OUT_XDATA,
  output IR_LD_XDATA,
  output MBR_LD_XDATA,
  output MBR_OUT_XDATA,
  output MBR_LD_CDATA,
  output MBR_OUT_CDATA,
  output MARL_LD_CADDRL,
  output MARH_LD_CADDRH,
  output PC_INC,
  output PC_REL_CDATA,
  output PCL_LD_CDATA,
  output PCL_OUT_CDATA,
  output PCH_LD_CDATA,
  output PCH_OUT_CDATA,
  output PC_OUT_CADDR,
  output STASHL_LD_CDATA,
  output STASHL_OUT_CDATA,
  output STASHH_LD_CDATA,
  output STASHH_OUT_CDATA,
  output A_LD_CDATA,
  output A_OUT_CDATA,
  output X_LD_CDATA,
  output X_OUT_CDATA,
  output Y_LD_CDATA,
  output Y_OUT_CDATA,
  output PN_LD,
  output PV_LD,
  output PZ_LD,
  output PC_LD,
  output P_SRC_0,
  output P_SRC_1,
  output ALUA_LD_CDATA,
  output ALUB_LD_CDATA,
  output ALUC_LD,
  output ALUR_OUT_CDATA,
  output ALUOP_0,
  output ALUOP_1,
  output ALUOP_2,
  output S_INC,
  output S_DEC,
  output S_LD_CDATA,
  output S_OUT_CDATA,
  output S_OUT_CADDR,
  output ALUC_SRC_0,
  output ALUC_SRC_1,
  output CUP_SRC_ALU,
  output ALUOP_3,
  output PC_RESET,
  output P_SRC_2,
  output P_OUT_CDATA,
  output P_IRQ,
  output ERR,
  output PI_LD
);

  wire and_1_out, and_2_out, and_3_out, and_4_out, and_5_out, and_6_out, not_1_out, not_2_out, uCJMP,
       uIRQINIT, uJMP, uJMPINV, uNJMP, uP0, uP0INIT, uP1, uP2, uVJMP, uZJMP, xor_1_out, xor_2_out, xor_3_out,
       xor_4_out;
  wire [15:0] add_1_s, IRQ_uCode_q, multiplexer_2_out, p0__Fetch_q;
  wire [15:5] uCode_5_d;

  Seven_Seg_Hex seven_seg_hex_1 (.d(lt_uCAR_gt[15:12]), .dp(1'b0));
  Seven_Seg_Hex seven_seg_hex_2 (.d(lt_uParam_gt[15:12]), .dp(1'b0));
  Seven_Seg_Hex seven_seg_hex_3 (.d(lt_uCAR_gt[7:4]), .dp(1'b0));
  Seven_Seg_Hex seven_seg_hex_4 (.d(lt_uCAR_gt[11:8]), .dp(1'b0));
  Seven_Seg_Hex seven_seg_hex_5 (.d(lt_uParam_gt[7:4]), .dp(1'b0));
  Seven_Seg_Hex seven_seg_hex_6 (.d(lt_uParam_gt[11:8]), .dp(1'b0));
  LED led_1 (.in(lt_uNEXTMUX_gt[1]));
  LED led_2 (.in(lt_uNEXTMUX_gt[2]));
  Seven_Seg_Hex seven_seg_hex_7 (.d(lt_uCAR_gt[3:0]), .dp(1'b0));
  Seven_Seg_Hex seven_seg_hex_8 (.d(lt_uParam_gt[3:0]), .dp(1'b0));
  LED led_3 (.in(lt_uNEXTMUX_gt[0]));
  Seven_Seg_Hex seven_seg_hex_9 (.d(lt_uNEXTCAR_gt[11:8]), .dp(1'b0));
  Seven_Seg_Hex seven_seg_hex_10 (.d(lt_uNEXTCAR_gt[15:12]), .dp(1'b0));
  Seven_Seg_Hex seven_seg_hex_11 (.d(lt_uNEXTCAR_gt[3:0]), .dp(1'b0));
  Seven_Seg_Hex seven_seg_hex_12 (.d(lt_uNEXTCAR_gt[7:4]), .dp(1'b0));
  Comparator #(.Bits(16)) comparator_1 (.a(lt_uCAR_gt), .b({16{1'b1}}), .eq(ERR));  // open: gt, lt
  ROM #(.AddrBits(16), .Bits(16)) uCode0 (.A(lt_uCAR_gt), .sel(1'b1), .D(lt_uParam_gt));
  ROM #(.AddrBits(16), .Bits(16)) uCode1 (
    .A(lt_uCAR_gt), .sel(1'b1),
    .D({MEM_LD_XDATA, CD_TO_CADDRH, CDATA_TO_CADDRL, CDATA_LD_FF, CDATA_LD_0, HALT, uJMPINV, uCJMP, uZJMP, uVJMP, uNJMP, uJMP, uP2, uP1, uP0, uP0INIT}));
  ROM #(.AddrBits(16), .Bits(16)) uCode2 (
    .A(lt_uCAR_gt), .sel(1'b1),
    .D({STASHL_LD_CDATA, PC_OUT_CADDR, PCH_OUT_CDATA, PCH_LD_CDATA, PCL_OUT_CDATA, PCL_LD_CDATA, PC_REL_CDATA, PC_INC, MARH_LD_CADDRH, MARL_LD_CADDRL, MBR_OUT_CDATA, MBR_LD_CDATA, MBR_OUT_XDATA, MBR_LD_XDATA, IR_LD_XDATA, MEM_OUT_XDATA}));
  ROM #(.AddrBits(16), .Bits(16)) uCode3 (
    .A(lt_uCAR_gt), .sel(1'b1),
    .D({ALUA_LD_CDATA, P_SRC_1, P_SRC_0, PC_LD, PZ_LD, PV_LD, PN_LD, Y_OUT_CDATA, Y_LD_CDATA, X_OUT_CDATA, X_LD_CDATA, A_OUT_CDATA, A_LD_CDATA, STASHH_OUT_CDATA, STASHH_LD_CDATA, STASHL_OUT_CDATA}));
  ROM #(.AddrBits(16), .Bits(16)) uCode4 (
    .A(lt_uCAR_gt), .sel(1'b1),
    .D({PC_RESET, ALUOP_3, CUP_SRC_ALU, ALUC_SRC_1, ALUC_SRC_0, S_OUT_CADDR, S_OUT_CDATA, S_LD_CDATA, S_DEC, S_INC, ALUOP_2, ALUOP_1, ALUOP_0, ALUR_OUT_CDATA, ALUC_LD, ALUB_LD_CDATA}));
  ROM #(.AddrBits(16), .Bits(16)) uCode_5 (
    .A(lt_uCAR_gt), .sel(1'b1), .D({uCode_5_d, PI_LD, uIRQINIT, P_IRQ, P_OUT_CDATA, P_SRC_2}));
  and and_1 (and_1_out, not_1_out, IRQ, uP0);
  not not_1 (not_1_out, Iin);
  Register #(.Bits(16)) uCAR (.D(lt_uNEXTCAR_gt), .C(ClockIn), .en(1'b1), .Q(lt_uCAR_gt));
  Add #(.Bits(16)) add_1 (.a(lt_uCAR_gt), .b(16'h1), .c_i(1'b0), .s(add_1_s));  // open: c_o
  or or_1 (lt_uNEXTMUX_gt[2], and_1_out, uJMP, and_2_out, and_3_out, and_4_out, and_5_out);
  and and_2 (and_2_out, uZJMP, xor_1_out);
  xor xor_1 (xor_1_out, Zin, uJMPINV);
  Register #(.Bits(16)) p0__Fetch (.D(lt_uParam_gt), .C(ClockIn), .en(uP0INIT), .Q(p0__Fetch_q));
  Register #(.Bits(16)) IRQ_uCode (.D(lt_uParam_gt), .C(ClockIn), .en(uIRQINIT), .Q(IRQ_uCode_q));
  and and_3 (and_3_out, uNJMP, xor_2_out);
  xor xor_2 (xor_2_out, Nin, uJMPINV);
  and and_4 (and_4_out, uVJMP, xor_3_out);
  xor xor_3 (xor_3_out, Vin, uJMPINV);
  Multiplexer #(.Bits(16)) multiplexer_1 (
    .sel(RESET), .in_0(multiplexer_2_out), .in_1({16{1'b0}}), .out(lt_uNEXTCAR_gt));
  Multiplexer #(.Selector_Bits(3), .Bits(16)) multiplexer_2 (
    .sel(lt_uNEXTMUX_gt), .in_0(add_1_s), .in_1(p0__Fetch_q), .in_2(DEMODEin), .in_3(DEOPCODEin),
    .in_4(lt_uParam_gt), .in_5(IRQ_uCode_q), .in_6({16{1'b0}}), .in_7({16{1'b0}}), .out(multiplexer_2_out));
  or or_2 (lt_uNEXTMUX_gt[1], uP1, uP2);
  and and_5 (and_5_out, uCJMP, xor_4_out);
  xor xor_4 (xor_4_out, Cin, uJMPINV);
  or or_3 (lt_uNEXTMUX_gt[0], uP0, uP2, and_6_out);
  and and_6 (and_6_out, not_2_out, IRQ, uP0);
  not not_2 (not_2_out, Iin);

  // Other names for the same wires on the sheet: PC_IRQ = P_IRQ; uNextMux[2:0] = lt_uNEXTMUX_gt;
  //   CDATA_TO_CADDRH = CD_TO_CADDRH; Clock = ClockIn; DECODEDMODEin[15:0] = DEMODEin;
  //   DECODEDOPCODEin[15:0] = DEOPCODEin; uCAR[15:0] = lt_uCAR_gt; uNextCAR[15:0] = lt_uNEXTCAR_gt;
  //   uParam[15:0] = lt_uParam_gt

  // Notes on the sheet:
  //   DEMODEin: default 169
  //   DEOPCODEin: default 169
  //   CAR
  //   uNextAddr
  //   NextMux
  //   Next
  //   Next Mux
  //   0 0 0 +1
  //   0 0 1 p0 (0)
  //   0 1 0 p1
  //   0 1 1 p2
  //   1 X X uJMPs
  //   Debug
  //   contents of uCode0 (hex, n*v repeats v):
  //   6000000,18000000,6000000,30000000,c0000000
  //   contents of uCode1 (hex, n*v repeats v):
  //   6000000,18000000,6000000,30000000,c0000000
  //   contents of uCode2 (hex, n*v repeats v):
  //   6000000,18000000,6000000,30000000,c0000000
  //   contents of uCode3 (hex, n*v repeats v):
  //   6000000,18000000,6000000,30000000,c0000000
  //   contents of uCode4 (hex, n*v repeats v):
  //   6000000,18000000,6000000,30000000,c0000000
  //   contents of uCode_5 (hex, n*v repeats v):
  //   6000000,18000000,6000000,30000000,c0000000
  //   Next Mux
  //   0 0 0 +1
  //   0 0 1 p0
  //   0 1 0 p1
  //   0 1 1 p2
  //   1 0 0 uJMPs
  //   1 0 1 IRQ
endmodule
