// Digital circuit Latched ALU.dig as structural Verilog
module Latched_ALU (
  input  CLOCK,
  input  [7:0] A,
  input  [7:0] B,
  input  CIN,
  input  LDA,
  input  LDB,
  input  LDC,
  input  [3:0] OP,
  output N,
  output V,
  output Z,
  output C,
  output [7:0] R,
  output [7:0] lt_A_gt,
  output [7:0] lt_B_gt,
  output lt_C_gt
);

  wire ALU_cout, ALU_vout, Cin_t, Shifter_cout;
  wire [7:0] ALU_out, Shifter_q;

  Register #(.Bits(8)) u_A (.D(A), .C(CLOCK), .en(LDA), .Q(lt_A_gt));
  Register #(.Bits(8)) u_B (.D(B), .C(CLOCK), .en(LDB), .Q(lt_B_gt));
  Register u_C (.D(Cin_t), .C(CLOCK), .en(LDC), .Q(lt_C_gt));
  Shifter Shifter (.D(lt_A_gt), .OP(OP[1]), .DIR(OP[0]), .Cin(lt_C_gt), .Q(Shifter_q), .COUT(Shifter_cout));
  ALU ALU (.A(lt_A_gt), .B(lt_B_gt), .OP(OP[2:0]), .CIN(lt_C_gt), .OUT(ALU_out), .VOUT(ALU_vout), .COUT(ALU_cout));
  Multiplexer #(.Bits(8)) multiplexer_1 (.sel(OP[3]), .in_0(ALU_out), .in_1(Shifter_q), .out({N, R[6:0]}));
  Comparator #(.Bits(8)) comparator_1 (.a({N, R[6:0]}), .b({8{1'b0}}), .eq(Z));  // open: gt, lt
  Multiplexer multiplexer_2 (.sel(OP[3]), .in_0(ALU_vout), .in_1(1'b0), .out(V));
  Multiplexer multiplexer_3 (.sel(OP[3]), .in_0(ALU_cout), .in_1(Shifter_cout), .out(C));

  assign R[7] = N;

  // Notes on the sheet:
  //   ALU operation
  //   0 0 0 0 AND
  //   0 0 0 1 OR
  //   0 0 1 0 NOT
  //   0 0 1 1 XOR
  //   0 1 0 0 ADD
  //   0 1 0 1 SUB
  //   0 1 1 0 INC
  //   0 1 1 1 DEC
  //   1 0  0 0 SHIFT-R
  //   1 0 0 1 SHIFT-L
  //   1 0 1 0 ROT-R
  //   1 0 1 1 ROT-L
endmodule
