// Digital circuit PC.dig as structural Verilog
module PC (
  input  LDH,
  input  LDL,
  input  INC,
  input  REL,
  input  [7:0] D,
  input  C,
  input  RESET,
  input  IRQ,
  output [7:0] QH,
  output [7:0] QL
);

  wire and_1_out, or_3_out, or_6_out, PCADDL_c_o;
  wire [1:0] or_2_out, or_4_out;
  wire [7:0] multiplexer_1_out, multiplexer_2_out, multiplexer_3_out, multiplexer_4_out, PCADDH_s, PCADDL_s;

  or or_1 (or_2_out[1], IRQ, RESET);
  Multiplexer #(.Selector_Bits(2), .Bits(8)) multiplexer_1 (
    .sel(or_2_out), .in_0(PCADDH_s), .in_1(D), .in_2({8{1'b1}}), .in_3({8{1'b1}}), .out(multiplexer_1_out));
  or or_2 (or_2_out[0], IRQ, LDH);
  or or_3 (or_3_out, INC, REL, LDH, RESET, IRQ);
  and and_1 (and_1_out, D[7], REL);
  Register #(.Bits(8)) PCH (.D(multiplexer_1_out), .C(C), .en(or_3_out), .Q(QH));
  Multiplexer #(.Bits(8)) multiplexer_2 (.sel(and_1_out), .in_0({8{1'b0}}), .in_1({8{1'b1}}), .out(multiplexer_2_out));
  Add #(.Bits(8)) PCADDH (.a(QH), .b(multiplexer_2_out), .c_i(PCADDL_c_o), .s(PCADDH_s));  // open: c_o
  or or_4 (or_4_out[1], IRQ, RESET);
  Multiplexer #(.Selector_Bits(2), .Bits(8)) multiplexer_3 (
    .sel(or_4_out), .in_0(PCADDL_s), .in_1(D), .in_2(8'hfc), .in_3(8'hfe), .out(multiplexer_3_out));
  or or_5 (or_4_out[0], IRQ, LDL);
  Multiplexer #(.Bits(8)) multiplexer_4 (.sel(INC), .in_0(D), .in_1(8'h1), .out(multiplexer_4_out));
  Add #(.Bits(8)) PCADDL (.a(QL), .b(multiplexer_4_out), .c_i(1'b0), .s(PCADDL_s), .c_o(PCADDL_c_o));
  or or_6 (or_6_out, INC, REL, LDL, RESET, IRQ);
  Register #(.Bits(8)) PCL (.D(multiplexer_3_out), .C(C), .en(or_6_out), .Q(QL));
endmodule
