// Digital circuit PC.dig as structural Verilog
module PC (
  input  LD,
  input  INC,
  input  REL,
  input  [7:0] D,
  input  C,
  output [7:0] Q
);

  wire _74377_1_pin1, Adder_High_pin2, Adder_High_pin6, Adder_High_pin11, Adder_High_pin15, Adder_Low_pin2,
       Adder_Low_pin6, Adder_Low_pin9, Adder_Low_pin11, Adder_Low_pin15, OR_pin3, OR_pin6,
       PC_IN_HIGH_MUX_pin4, PC_IN_HIGH_MUX_pin7, PC_IN_HIGH_MUX_pin9, PC_IN_HIGH_MUX_pin12,
       PC_IN_LOW_MUX_pin4, PC_IN_LOW_MUX_pin7, PC_IN_LOW_MUX_pin9, PC_IN_LOW_MUX_pin12, S0, S1, S2, S3, S4,
       S5, S6, S7;

  Seven_Seg_Hex seven_seg_hex_1 (.d(Q[3:0]), .dp(1'b0));
  Seven_Seg_Hex seven_seg_hex_2 (.d(Q[7:4]), .dp(1'b0));
  LED led_1 (.in(LD));
  LED led_2 (.in(INC));
  LED led_3 (.in(REL));
  _74157 PC_IN_LOW_MUX (
    .pin1(LD), .pin2(S0), .pin3(D[0]), .pin4(PC_IN_LOW_MUX_pin4), .pin5(S1), .pin6(D[1]),
    .pin7(PC_IN_LOW_MUX_pin7), .pin8(1'b0), .pin9(PC_IN_LOW_MUX_pin9), .pin10(D[2]), .pin11(S2),
    .pin12(PC_IN_LOW_MUX_pin12), .pin13(D[3]), .pin14(S3), .pin15(1'b0), .pin16(1'b1));
  _74157 PC_IN_HIGH_MUX (
    .pin1(LD), .pin2(S4), .pin3(D[4]), .pin4(PC_IN_HIGH_MUX_pin4), .pin5(S5), .pin6(D[5]),
    .pin7(PC_IN_HIGH_MUX_pin7), .pin8(1'b0), .pin9(PC_IN_HIGH_MUX_pin9), .pin10(D[6]), .pin11(S6),
    .pin12(PC_IN_HIGH_MUX_pin12), .pin13(D[7]), .pin14(S7), .pin15(1'b0), .pin16(1'b1));
  _7432 OR (
    .pin1(REL), .pin2(LD), .pin3(OR_pin3), .pin4(OR_pin3), .pin5(INC), .pin6(OR_pin6), .pin7(1'b0),
    .pin9(1'b0), .pin10(1'b0), .pin12(1'b0), .pin13(1'b0), .pin14(1'b1));  // open: pin8, pin11
  _74377 _74377_1 (
    .pin1(_74377_1_pin1), .pin2(Q[0]), .pin3(PC_IN_LOW_MUX_pin4), .pin4(PC_IN_LOW_MUX_pin7), .pin5(Q[1]),
    .pin6(Q[2]), .pin7(PC_IN_LOW_MUX_pin9), .pin8(PC_IN_LOW_MUX_pin12), .pin9(Q[3]), .pin10(1'b0), .pin11(C),
    .pin12(Q[4]), .pin13(PC_IN_HIGH_MUX_pin4), .pin14(PC_IN_HIGH_MUX_pin7), .pin15(Q[5]), .pin16(Q[6]),
    .pin17(PC_IN_HIGH_MUX_pin9), .pin18(PC_IN_HIGH_MUX_pin12), .pin19(Q[7]), .pin20(1'b1));
  _7404 _7404_1 (
    .pin1(OR_pin6), .pin2(_74377_1_pin1), .pin3(1'b0), .pin5(1'b0), .pin7(1'b0), .pin9(1'b0), .pin11(1'b0),
    .pin13(1'b0), .pin14(1'b1));  // open: pin4, pin6, pin8, pin10, pin12
  _74283 Adder_Low (
    .pin1(S1), .pin2(Adder_Low_pin2), .pin3(Q[1]), .pin4(S0), .pin5(Q[0]), .pin6(Adder_Low_pin6),
    .pin7(1'b0), .pin8(1'b0), .pin9(Adder_Low_pin9), .pin10(S3), .pin11(Adder_Low_pin11), .pin12(Q[3]),
    .pin13(S2), .pin14(Q[2]), .pin15(Adder_Low_pin15), .pin16(1'b1));
  _74283 Adder_High (
    .pin1(S5), .pin2(Adder_High_pin2), .pin3(Q[5]), .pin4(S4), .pin5(Q[4]), .pin6(Adder_High_pin6),
    .pin7(Adder_Low_pin9), .pin8(1'b0), .pin10(S6), .pin11(Adder_High_pin11), .pin12(Q[7]), .pin13(S7),
    .pin14(Q[6]), .pin15(Adder_High_pin15), .pin16(1'b1));  // open: pin9
  _74157 Adder_Low_Input_Mux (
    .pin1(INC), .pin2(D[0]), .pin3(1'b1), .pin4(Adder_Low_pin6), .pin5(D[1]), .pin6(1'b0),
    .pin7(Adder_Low_pin2), .pin8(1'b0), .pin9(Adder_Low_pin15), .pin10(1'b0), .pin11(D[2]),
    .pin12(Adder_Low_pin11), .pin13(1'b0), .pin14(D[3]), .pin15(1'b0), .pin16(1'b1));
  _74157 Adder_High_Input_Mux (
    .pin1(INC), .pin2(D[4]), .pin3(1'b0), .pin4(Adder_High_pin6), .pin5(D[5]), .pin6(1'b0),
    .pin7(Adder_High_pin2), .pin8(1'b0), .pin9(Adder_High_pin15), .pin10(1'b0), .pin11(D[6]),
    .pin12(Adder_High_pin11), .pin13(1'b0), .pin14(D[7]), .pin15(1'b0), .pin16(1'b1));

  // Notes on the sheet:
  //   Selects either the incoming D (for LD)
  //   or the result of the add operation
  //   (INC or REL) to send to PC register.
  //   Adds either D (Relateive signed value)  
  //   or 1 to PC
  //   Selects between
  //   1 - For INC
  //   D - For LD and REL
endmodule
