// Digital circuit Register.dig as structural Verilog
module Register (
  input  C,
  input  [7:0] D,
  input  OUT,
  input  LD,
  output [7:0] Q,
  output [7:0] lt_Q_gt
);

  wire _7404_1_pin12, _74377_1_pin1, Tri_State_pin2, Tri_State_pin4, Tri_State_pin6, Tri_State_pin8,
       Tri_State_pin11, Tri_State_pin13, Tri_State_pin15, Tri_State_pin17;

  Seven_Seg_Hex seven_seg_hex_1 (.d(Q[7:4]), .dp(1'b0));
  Seven_Seg_Hex seven_seg_hex_2 (.d(Q[3:0]), .dp(1'b0));
  Seven_Seg_Hex seven_seg_hex_3 (.d(lt_Q_gt[7:4]), .dp(1'b0));
  Seven_Seg_Hex seven_seg_hex_4 (.d(lt_Q_gt[3:0]), .dp(1'b0));
  _74244 Tri_State (
    .pin1(1'b0), .pin2(Tri_State_pin2), .pin3(lt_Q_gt[7]), .pin4(Tri_State_pin4), .pin5(lt_Q_gt[6]),
    .pin6(Tri_State_pin6), .pin7(lt_Q_gt[5]), .pin8(Tri_State_pin8), .pin9(lt_Q_gt[4]), .pin10(1'b0),
    .pin11(Tri_State_pin11), .pin12(lt_Q_gt[3]), .pin13(Tri_State_pin13), .pin14(lt_Q_gt[2]),
    .pin15(Tri_State_pin15), .pin16(lt_Q_gt[1]), .pin17(Tri_State_pin17), .pin18(lt_Q_gt[0]), .pin19(1'b0),
    .pin20(1'b1));
  _74377 _74377_1 (
    .pin1(_74377_1_pin1), .pin2(Tri_State_pin2), .pin3(D[0]), .pin4(D[1]), .pin5(Tri_State_pin4),
    .pin6(Tri_State_pin6), .pin7(D[2]), .pin8(D[3]), .pin9(Tri_State_pin8), .pin10(1'b0), .pin11(C),
    .pin12(Tri_State_pin11), .pin13(D[4]), .pin14(D[5]), .pin15(Tri_State_pin13), .pin16(Tri_State_pin15),
    .pin17(D[6]), .pin18(D[7]), .pin19(Tri_State_pin17), .pin20(1'b1));
  _7404 _7404_1 (
    .pin1(LD), .pin2(_74377_1_pin1), .pin3(1'b0), .pin5(1'b0), .pin7(1'b0), .pin9(1'b0), .pin11(1'b0),
    .pin12(_7404_1_pin12), .pin13(OUT), .pin14(1'b1));  // open: pin4, pin6, pin8, pin10
  _74244 Tri_State_2 (
    .pin1(_7404_1_pin12), .pin2(Tri_State_pin2), .pin3(Q[7]), .pin4(Tri_State_pin4), .pin5(Q[6]),
    .pin6(Tri_State_pin6), .pin7(Q[5]), .pin8(Tri_State_pin8), .pin9(Q[4]), .pin10(1'b0),
    .pin11(Tri_State_pin11), .pin12(Q[3]), .pin13(Tri_State_pin13), .pin14(Q[2]), .pin15(Tri_State_pin15),
    .pin16(Q[1]), .pin17(Tri_State_pin17), .pin18(Q[0]), .pin19(_7404_1_pin12), .pin20(1'b1));

  // Other names for the same wires on the sheet: lt_Q0_gt = lt_Q_gt[0]; lt_Q1_gt = lt_Q_gt[1]; lt_Q2_gt = lt_Q_gt[2];
  //   lt_Q3_gt = lt_Q_gt[3]; lt_Q4_gt = lt_Q_gt[4]; lt_Q5_gt = lt_Q_gt[5]; lt_Q6_gt = lt_Q_gt[6];
  //   lt_Q7_gt = lt_Q_gt[7]

  // Notes on the sheet:
  //   Q
  //   <Q>
endmodule
